# Fritzing sketch Untitled Sketch (saved by Fritzing 0.8.7b)
breadboards: 1

parts:
  Parte1 = Arduino Due (Rev2b)  # not connected
  Power_RGB1 = Prolight RGB 3 Watt Star  # not connected
  LCD1 = LCD screen  # not connected
  S1 = Pushbutton [package="[THT]"]
  S2 = Pushbutton [package="[THT]"]
  T1 = LM35 Temperature Sensor [package="TO92 [THT]"]  # not connected
  R1 = Trimmer Potentiometer [maximum_resistance=10kΩ package=THT]  # not connected
  Parte2 = Real Time Clock Module - DS1307 RTC Breakout Board  # not connected
  U1 = ZXLD1360 [package=sot23-5]  # not connected
  U2 = ZXLD1360 [package=sot23-5]  # not connected
  U3 = ZXLD1360 [package=sot23-5]  # not connected
  U4 = ZXLD1360 [package=sot23-5]  # not connected
  U5 = ZXLD1360 [package=sot23-5]  # not connected
  U6 = ZXLD1360 [package=sot23-5]  # not connected
  Power_RGB2 = Prolight RGB 3 Watt Star  # not connected
  Power_RGB3 = Prolight RGB 3 Watt Star  # not connected
  Power_RGB4 = Prolight RGB 3 Watt Star  # not connected
  Power_RGB5 = Prolight RGB 3 Watt Star  # not connected
  Power_RGB6 = Prolight RGB 3 Watt Star  # not connected
  Power_RGB7 = Prolight RGB 3 Watt Star  # not connected
  Power_RGB8 = Prolight RGB 3 Watt Star  # not connected
  Power_RGB9 = Prolight RGB 3 Watt Star  # not connected
  Power_RGB10 = Prolight RGB 3 Watt Star  # not connected
  Power_RGB11 = Prolight RGB 3 Watt Star  # not connected
  Power_RGB12 = Prolight RGB 3 Watt Star  # not connected

nets:
  N1: S1.Pin_1, S1.Pin_2
  N2: S1.Pin_3, S1.Pin_4
  N3: S2.Pin_1, S2.Pin_2
  N4: S2.Pin_3, S2.Pin_4
